// Logisim project CS1501_U201514477_华龙_cpu.circ as structural Verilog: 4 circuits, main circuit MIPS CPU
module MIPS_CPU (
);

  wire registerfile_1_p2, registerfile_1_p4;
  wire [23:0] PC_q_2;
  wire [31:0] PC_q, rom_1_data;

  Register #(.width(32)) PC (.Q({PC_q[31:26], PC_q_2, PC_q[1:0]}));  // open: D, en, clk, clr
  PC_1 pc_1_1 ();  // open: PC, PC_4
  ROM #(.addrWidth(24), .dataWidth(32)) rom_1 (.addr(PC_q_2), .data(rom_1_data));  // open: sel
  Sign_Extend sign_extend_1 ();  // open: _17bit, _32bit
  // RegisterFile registerfile_1: pin names not known; wires that end beside it: rom_1_data, registerfile_1_p2, registerfile_1_p2, registerfile_1_p4, registerfile_1_p4
  // ALU alu_1: pin names not known
  // MIPS_RAM mips_ram_1: pin names not known
endmodule

module PC_1 (
  input  [31:0] PC,
  output [31:0] PC_4
);

  // Incrementer incrementer_1: pin names not known; wires that end beside it: PC[31:2], PC_4[31:2]

  assign PC_4[1:0] = PC[1:0];
endmodule

module Sign_Extend (
  input  [16:0] _17bit,
  output [31:0] _32bit
);


  assign _32bit = {{16{_17bit[16]}}, _17bit[15:0]};
endmodule

module \_8位数码管显示  (
);

  wire [31:0] undriven, \数码管锁存_q ;

  Register #(.width(32)) \u_数码管锁存  (.D(undriven), .Q(\数码管锁存_q ));  // open: en, clk, clr
  Hex_Digit_Display hex_digit_display_1 (.value(\数码管锁存_q [31:28]));  // open: dp
  Hex_Digit_Display hex_digit_display_2 (.value(\数码管锁存_q [27:24]));  // open: dp
  Hex_Digit_Display hex_digit_display_3 (.value(\数码管锁存_q [23:20]));  // open: dp
  Hex_Digit_Display hex_digit_display_4 (.value(\数码管锁存_q [19:16]));  // open: dp
  Hex_Digit_Display hex_digit_display_5 (.value(\数码管锁存_q [11:8]));  // open: dp
  Hex_Digit_Display hex_digit_display_6 (.value(\数码管锁存_q [15:12]));  // open: dp
  Hex_Digit_Display hex_digit_display_7 (.value(\数码管锁存_q [3:0]));  // open: dp
  Hex_Digit_Display hex_digit_display_8 (.value(\数码管锁存_q [7:4]));  // open: dp
endmodule
